// Logisim project SAP-1.circ as structural Verilog: 13 circuits, main circuit main
module main (
  input  [7:0] in_1,
  input  La,
  input  Ea
);

  wire [7:0] accumulator_out_3;

  TTL_adder_subtractor ttl_adder_subtractor_1 (.a(accumulator_out_3));  // open: b, sub, sum, carry_out
  accumulator accumulator (.X(in_1), .LOAD(La), .out_3(accumulator_out_3));
endmodule

module _4_bit_adder_subtractor (
  input  [3:0] a,
  input  [3:0] b,
  input  sub,
  output [3:0] sum,
  output carry_out
);

  wire full_adder_2_carry_out, full_adder_3_carry_out, full_adder_carry_out, xor_1_out, xor_2_out, xor_3_out,
       xor_4_out;

  xor xor_1 (xor_1_out, b[0], sub);
  xor xor_2 (xor_2_out, b[1], sub);
  xor xor_3 (xor_3_out, b[2], sub);
  xor xor_4 (xor_4_out, b[3], sub);
  full_adder full_adder (.a(a[0]), .b(xor_1_out), .c(sub), .sum(sum[0]), .carry_out(full_adder_carry_out));
  full_adder full_adder_2 (
    .a(a[1]), .b(xor_2_out), .c(full_adder_carry_out), .sum(sum[1]), .carry_out(full_adder_2_carry_out));
  full_adder full_adder_3 (
    .a(a[2]), .b(xor_3_out), .c(full_adder_2_carry_out), .sum(sum[2]), .carry_out(full_adder_3_carry_out));
  full_adder full_adder_4 (.a(a[3]), .b(xor_4_out), .c(full_adder_3_carry_out), .sum(sum[3]), .carry_out(carry_out));
endmodule

module full_adder (
  input  a,
  input  b,
  input  c,
  output sum,
  output carry_out
);

  wire and_1_out, and_2_out, xor_1_out, xor_2_out;

  xor xor_1 (xor_1_out, b, c);
  and and_1 (and_1_out, a, b);
  xor xor_2 (xor_2_out, a, b);
  xor xor_3 (sum, a, xor_1_out);
  and and_2 (and_2_out, xor_2_out, c);
  or or_1 (carry_out, and_1_out, and_2_out);
endmodule

module TTL_adder_subtractor (
  input  [7:0] a,
  input  [7:0] b,
  input  sub,
  output [7:0] sum,
  output carry_out
);

  wire _4_bit_adder_subtractor_carry_out, full_adder_2_carry_out, full_adder_3_carry_out,
       full_adder_carry_out, xor_1_out, xor_2_out, xor_3_out, xor_4_out;

  _4_bit_adder_subtractor _4_bit_adder_subtractor (
    .a(a[3:0]), .b(b[3:0]), .sub(sub), .sum(sum[3:0]), .carry_out(_4_bit_adder_subtractor_carry_out));
  xor xor_1 (xor_1_out, b[4], sub);
  xor xor_2 (xor_2_out, b[5], sub);
  xor xor_3 (xor_3_out, b[6], sub);
  xor xor_4 (xor_4_out, b[7], sub);
  full_adder full_adder (
    .a(a[4]), .b(xor_1_out), .c(_4_bit_adder_subtractor_carry_out), .sum(sum[4]),
    .carry_out(full_adder_carry_out));
  full_adder full_adder_2 (
    .a(a[5]), .b(xor_2_out), .c(full_adder_carry_out), .sum(sum[5]), .carry_out(full_adder_2_carry_out));
  full_adder full_adder_3 (
    .a(a[6]), .b(xor_3_out), .c(full_adder_2_carry_out), .sum(sum[6]), .carry_out(full_adder_3_carry_out));
  full_adder full_adder_4 (.a(a[7]), .b(xor_4_out), .c(full_adder_3_carry_out), .sum(sum[7]), .carry_out(carry_out));
endmodule

module Buffer_register (
  input  [3:0] X,
  input  LOAD,
  input  CLR,
  input  [3:0] in_4,
  output out_5
);

  wire and_1_out, and_2_out, clock_1_out, not_1_out, or_1_out;

  Clock clock_1 (.out(clock_1_out));
  not not_1 (not_1_out, LOAD);
  and and_1 (and_1_out, LOAD, X[3]);
  or or_1 (or_1_out, and_1_out, and_2_out);
  and and_2 (and_2_out, not_1_out, in_4[3]);
  edge_triggered_D_flip_flop edge_triggered_d_flip_flop_1 (
    .PRESET(or_1_out), .D(CLR), .CLEAR(clock_1_out), .Q(in_4[3]));  // open: Q_prime
endmodule

module D_flip_flop (
  input  D,
  input  CLK,
  input  CLEAR,
  output Q,
  output Q_prime
);

  wire and_1_out, and_2_out, nand_1_out, nand_2_out, not_1_out;

  not not_1 (not_1_out, D);
  nand nand_1 (nand_1_out, D, CLK);
  nand nand_2 (nand_2_out, CLK, not_1_out);
  and and_1 (and_1_out, CLEAR, nand_1_out);
  and and_2 (and_2_out, nand_2_out, CLEAR);
  nor nor_1 (Q, and_1_out, Q_prime);
  nor nor_2 (Q_prime, Q, and_2_out);
endmodule

module edge_triggered_D_flip_flop (
  input  PRESET,
  input  D,
  input  CLEAR,
  output Q,
  output Q_prime
);

  wire clock_1_out, nand_1_out, nand_2_out, nand_3_out, nand_4_out;

  Clock clock_1 (.out(clock_1_out));
  nand nand_1 (nand_1_out, PRESET, nand_4_out, nand_2_out);
  nand nand_2 (nand_2_out, nand_1_out, CLEAR, clock_1_out);
  nand nand_3 (nand_3_out, nand_2_out, clock_1_out, nand_4_out);
  nand nand_4 (nand_4_out, nand_3_out, D, CLEAR);
  nor nor_1 (Q, PRESET, nand_2_out, Q_prime);
  nor nor_2 (Q_prime, Q, nand_3_out, CLEAR);
endmodule

module Controlled_buffer_register (
  input  [3:0] X,
  input  LOAD,
  input  CLK,
  input  CLEAR,
  output [3:0] out_5
);

  wire and_1_out, and_2_out, and_3_out, and_4_out, and_5_out, and_6_out, and_7_out, and_8_out, not_1_out,
       or_1_out, or_2_out, or_3_out, or_4_out;

  and and_1 (and_1_out, X[3], LOAD);
  and and_2 (and_2_out, not_1_out, out_5[3]);
  or or_1 (or_1_out, and_1_out, and_2_out);
  D_Flip_Flop d_ff_1 (.clk(CLK), .D(or_1_out), .Q(out_5[3]), .preset(CLEAR));  // open: Qn, en, reset
  and and_3 (and_3_out, X[2], LOAD);
  or or_2 (or_2_out, and_3_out, and_4_out);
  and and_4 (and_4_out, not_1_out, out_5[2]);
  D_Flip_Flop d_ff_2 (.clk(CLK), .D(or_2_out), .Q(out_5[2]), .preset(CLEAR));  // open: Qn, en, reset
  and and_5 (and_5_out, X[1], LOAD);
  and and_6 (and_6_out, not_1_out, out_5[1]);
  or or_3 (or_3_out, and_5_out, and_6_out);
  D_Flip_Flop d_ff_3 (.clk(CLK), .D(or_3_out), .Q(out_5[1]), .preset(CLEAR));  // open: Qn, en, reset
  and and_7 (and_7_out, X[0], LOAD);
  or or_4 (or_4_out, and_7_out, and_8_out);
  and and_8 (and_8_out, not_1_out, out_5[0]);
  D_Flip_Flop d_ff_4 (.clk(CLK), .D(or_4_out), .Q(out_5[0]), .preset(CLEAR));  // open: Qn, en, reset
  not not_1 (not_1_out, LOAD);
endmodule

module accumulator (
  input  [7:0] X,
  input  LOAD,
  output [7:0] out_3
);

  wire clock_1_out;

  Clock clock_1 (.out(clock_1_out));
  Controlled_buffer_register controlled_buffer_register_1 (
    .X(X[7:4]), .CLK(clock_1_out), .LOAD(LOAD), .out_5(out_3[7:4]));  // open: CLEAR
  Controlled_buffer_register controlled_buffer_register_2 (
    .X(X[3:0]), .CLK(clock_1_out), .LOAD(LOAD), .out_5(out_3[3:0]));  // open: CLEAR
endmodule

module b_register (
  input  [7:0] X,
  input  LOAD,
  output [7:0] out_3
);

  wire clock_1_out;

  Clock clock_1 (.out(clock_1_out));
  Controlled_buffer_register controlled_buffer_register_1 (
    .X(X[7:4]), .CLK(clock_1_out), .LOAD(LOAD), .out_5(out_3[7:4]));  // open: CLEAR
  Controlled_buffer_register controlled_buffer_register_2 (
    .X(X[3:0]), .CLK(clock_1_out), .LOAD(LOAD), .out_5(out_3[3:0]));  // open: CLEAR
endmodule

module output_register (
  input  [7:0] X,
  input  LOAD,
  output [7:0] out_3
);

  wire clock_1_out;

  Clock clock_1 (.out(clock_1_out));
  Controlled_buffer_register controlled_buffer_register_1 (
    .X(X[7:4]), .CLK(clock_1_out), .LOAD(LOAD), .out_5(out_3[7:4]));  // open: CLEAR
  Controlled_buffer_register controlled_buffer_register_2 (
    .X(X[3:0]), .CLK(clock_1_out), .LOAD(LOAD), .out_5(out_3[3:0]));  // open: CLEAR
endmodule

module program_counter (
  input  COUNT,
  input  CLK,
  input  CLR,
  output [3:0] out_4
);

  wire not_1_out, not_2_out, not_3_out, not_4_out, not_5_out;

  not not_1 (not_1_out, CLK);
  not not_2 (not_2_out, CLR);
  J_K_Flip_Flop j_k_ff_1 (
    .J(COUNT), .clk(not_1_out), .K(COUNT), .Q(out_4[0]), .reset(not_2_out));  // open: Qn, preset, en
  not not_3 (not_3_out, out_4[0]);
  J_K_Flip_Flop j_k_ff_2 (
    .J(COUNT), .clk(not_3_out), .K(COUNT), .Q(out_4[1]), .reset(not_2_out));  // open: Qn, preset, en
  not not_4 (not_4_out, out_4[1]);
  J_K_Flip_Flop j_k_ff_3 (
    .J(COUNT), .clk(not_4_out), .K(COUNT), .Q(out_4[2]), .reset(not_2_out));  // open: Qn, preset, en
  not not_5 (not_5_out, out_4[2]);
  J_K_Flip_Flop j_k_ff_4 (
    .J(COUNT), .clk(not_5_out), .K(COUNT), .Q(out_4[3]), .reset(not_2_out));  // open: Qn, preset, en
endmodule

module ring_counter (
  input  CLR
);

  wire clock_1_out, d_ff_1_q, d_ff_2_q, d_ff_3_q, d_ff_4_q, not_1_out;

  D_Flip_Flop d_ff_1 (.clk(clock_1_out), .D(d_ff_2_q), .Q(d_ff_1_q), .reset(not_1_out));  // open: Qn, preset, en
  D_Flip_Flop d_ff_2 (.clk(clock_1_out), .D(d_ff_3_q), .Q(d_ff_2_q), .reset(not_1_out));  // open: Qn, preset, en
  D_Flip_Flop d_ff_3 (.clk(clock_1_out), .D(d_ff_4_q), .Q(d_ff_3_q), .reset(not_1_out));  // open: Qn, preset, en
  D_Flip_Flop d_ff_4 (.clk(clock_1_out), .D(d_ff_1_q), .Q(d_ff_4_q), .preset(not_1_out));  // open: Qn, en, reset
  not not_1 (not_1_out, CLR);
  Clock clock_1 (.out(clock_1_out));
endmodule
